# Fritzing sketch 3x 7segment (saved by Fritzing 0.9.1b)
stripboards: 1

parts:
  J1 = shrouded pin header, 26 pins [form="♂ (shrouded male)"]
  J3 = longpad pin header, 5 pins [form="long pad"]
  J4 = longpad pin header, 5 pins [form="long pad"]
  J5 = male pin header, 1 pin [form="♂ (male)"]
  J6 = male pin header, 1 pin [form="♂ (male)"]
  J2 = longpad pin header, 5 pins [form="long pad"]

nets:
  N1: J1.pin10, J2.pin5
  N2: J1.pin12, J3.pin3, J4.pin3, J2.pin3
  N3: J1.pin15, J3.pin4, J4.pin4, J2.pin4
  N4: J1.pin24, J3.pin2, J4.pin2, J2.pin2
  N5: J1.pin26, J3.pin1, J4.pin1, J2.pin1
  N6: J3.pin5, J5.pin1
  N7: J4.pin5, J6.pin1
